# Fritzing sketch bb01v01 (saved by Fritzing 0.9.3b)
breadboards: 1

parts:
  U1 = Adafruit Trinket 5V
  D1 = NeoPixel Jewel [part_number=2226]
  D2 = NeoPixel Jewel [part_number=2226]
  R1 = Resistor [tolerance=±5% resistance=470 package="2010 [SMD]"]
  C1 = Electrolytic Capacitor [capacitance=1mF package="200 mil [THT, electrolytic]"]
  BATT1 = 3xAAA Switchable Battery Pack w/Bare Wire
  S1 = SPST Switch [package=switch-spdt_lock.007s]
  MIC1 = Microphone
  R4 = Resistor [tolerance=±5% resistance=10k package="0805 [SMD]"]
  S2 = Pushbutton [package="[THT]"]
  S3 = Pushbutton [package="[THT]"]
  R2 = Resistor [tolerance=±5% resistance=10k package="0805 [SMD]"]
  R3 = Resistor [tolerance=±5% resistance=10k package="0805 [SMD]"]

nets:
  VDD: U1.VBAT, D1.VDD, D2.VDD, C1.+, S1.O, S2.Pin_3, S2.Pin_4, S3.Pin_3, S3.Pin_4
  GND: U1.GND, D1.GND, D2.GND, C1.-, BATT1.NEG, S1.P, MIC1.pin1
  N1: U1.#1, S2.Pin_1, S2.Pin_2, R2.Pin_0
  N2: U1.#2, S3.Pin_1, S3.Pin_2, R3.Pin_0
  N3: U1.#4, R1.Pin_0
  N4: U1.#3, MIC1.pin2, R4.Pin_0
  N5: D1.IN, R1.Pin_1
  N6: D1.OUT, D2.IN
  N7: BATT1.POS, S1.S

custom parts:
  Adafruit Trinket 5V: Trinket may be small, but do not be fooled by its size! It's a tiny microcontroller board, built around the Atmel ATtiny85, a little chip with a lot of power. We wanted to design a microcontroller board that was small enough to fit into any project, and low cost enough to use without hesitation. Perfect for when you don't want to give up your expensive dev-board and you aren't willing to take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
  NeoPixel Jewel: We fit seven of our tiny 5050 (5mm x 5mm) smart RGB LEDs onto a beautiful, round PCB with mounting holes and a chainable design to create what we think is our most elegant (and evening-wear appropriate) NeoPixel board yet. Use only one microcontroller pin to control as many as you can chain together! Each LED is addressable as the driver chip is inside the LED. Each one has ~18mA constant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
  3xAAA Switchable Battery Pack w/Bare Wire: 3xAAA Switchable Battery Pack w/Bare Wire Connectors
